// Digital circuit Flip_Flop.dig as structural Verilog
module Flip_Flop (
  input  R,
  input  S,
  input  R_2,
  input  S_2
);

  wire and_1_out, and_2_out, not_1_out, not_2_out, or_1_out, or_2_out;

  not not_1 (not_1_out, R);
  not not_2 (not_2_out, R_2);
  or or_1 (or_1_out, and_2_out, S);
  and and_1 (and_1_out, or_2_out, not_2_out);
  and and_2 (and_2_out, or_1_out, not_1_out);
  or or_2 (or_2_out, and_1_out, S_2);
  LED led_1 (.in(and_2_out));
  LED led_2 ();  // open: in

  // Notes on the sheet:
  //   RS Flip Flop
  //   Rücksetzdominanz
  //   SR Flip Flop
  //   Setzdominanz
endmodule
