// Digital circuit Flips.dig as structural Verilog
module Flips (
  input  R,
  input  S,
  input  S_2,
  input  R_2,
  input  S_3,
  input  R_3,
  input  S_4,
  input  R_4
);

  wire and_1_out, and_2_out, nand_1_out, nand_2_out, nor_1_out, nor_2_out, not_1_out, not_2_out, not_3_out,
       not_4_out, or_1_out, or_2_out;

  not not_1 (not_1_out, R);
  not not_2 (not_2_out, R_2);
  or or_1 (or_1_out, and_2_out, S);
  and and_1 (and_1_out, or_2_out, not_2_out);
  not not_3 (not_3_out, S_4);
  not not_4 (not_4_out, R_4);
  and and_2 (and_2_out, or_1_out, not_1_out);
  or or_2 (or_2_out, and_1_out, S_2);
  nor nor_1 (nor_1_out, S_3, nor_2_out);
  nor nor_2 (nor_2_out, nor_1_out, R_3);
  nand nand_1 (nand_1_out, not_3_out, nand_2_out);
  nand nand_2 (nand_2_out, nand_1_out, not_4_out);
  LED led_1 (.in(and_2_out));
  LED led_2 (.in(or_2_out));
  LED nicht_Q (.in(nor_1_out));
  LED Q (.in(nor_2_out));
  LED Q_2 (.in(nand_1_out));
  LED nicht_Q_2 (.in(nand_2_out));

  // Notes on the sheet:
  //   RS Flip Flop
  //   Rücksetz Dominanz
  //   SR Flip Flop
  //   Setz Dominanz
endmodule
